# Fritzing sketch EnerginoBis (saved by Fritzing 0.7.5b)
breadboards: 1

parts:
  100k = Resistor [tolerance=±5% resistance=100k package=THT]
  -_IN_+ = Screw terminal - 2 pins [package=THT]
  10k = Resistor [tolerance=±5% resistance=10k package=THT]
  -_OUT_+ = Screw terminal - 2 pins [package=THT]
  Q1 = NPN-Transistor [package="TO92 [THT]"]
  1k = Resistor [tolerance=±5% resistance=1k package=THT]
  10k_2 = Resistor [tolerance=±5% resistance=10k package=THT]
  D1 = Rectifier Diode [part_number=1N4001 package="300 mil [THT]"]
  Energino_v1 = Arduino
  IC1 = IC, DIP package, 12 pins [chip_label=Relay spacing=300mil]
  ACS712_Low_Current = ACS712 Low Current Sensor Board v12
  Part2 = SO08 [chip_label=SOIC-14 spacing=300mil package=SO]  # not connected

nets:
  N1: 100k.Pin_0, 10k.Pin_1, Energino_v1.A1
  N2: 100k.Pin_1, -_IN_+.pin1, ACS712_Low_Current.IP-
  GND: -_IN_+.pin2, 10k.Pin_0, -_OUT_+.pin2, Q1.E, 10k_2.Pin_0, Energino_v1.GND, ACS712_Low_Current.GND
  N3: -_OUT_+.pin1, IC1.pin4
  N4: Q1.B, 1k.Pin_0, 10k_2.Pin_1
  N5: Q1.C, D1.anode, IC1.pin12
  N6: 1k.Pin_1, Energino_v1.D2
  +5V: D1.cathode, Energino_v1.+5V, IC1.pin7, ACS712_Low_Current.5V
  N7: Energino_v1.A0, ACS712_Low_Current.VO
  N8: IC1.pin1, ACS712_Low_Current.IP+
